// Logisim project ProcoLP.circ as structural Verilog
module CTL7 (
  input  [2:0] OP_in,
  input  [2:0] rA,
  output [2:0] OP_out,
  output [2:0] rT
);

  wire and_1_out, and_2_out, and_3_out, not_1_out;

  and and_1 (and_1_out, OP_in[2], ~OP_in[1], OP_in[0]);  // AND_Gate
  and and_2 (and_2_out, ~and_1_out, ~and_3_out);  // AND_Gate
  assign rT = and_2_out ? rA : 3'bz;  // Controlled_Buffer controlled_buffer_1
  and and_3 (and_3_out, OP_in[0], OP_in[1], ~OP_in[2]);  // AND_Gate
  not not_1 (not_1_out, and_2_out);
  assign rT = not_1_out ? 3'b000 : 3'bz;  // Controlled_Buffer controlled_buffer_2

  assign OP_out = OP_in;
endmodule

module CTL6 (
  input  [2:0] OP,
  output s2,
  output op0
);

  wire and_1_out, and_2_out;

  and and_1 (and_1_out, ~OP[0], ~OP[1], ~OP[2]);  // AND_Gate
  and and_2 (and_2_out, ~OP[0], OP[1], ~OP[2]);  // AND_Gate
  nand nand_1 (op0, ~OP[0], OP[1], OP[2]);  // NAND_Gate
  or or_1 (s2, and_1_out, and_2_out);
endmodule
